# Fritzing sketch Auto-farm (saved by Fritzing 0.9.5d)
breadboards: 2

parts:
  MCU1 = Raspberry Pi Zero
  GSM_SIM_GPSR_SMS_SIM900_SIM1 = SIM800L [package=THT]
  BMS = DC Power [voltage=5]
  DC-DC = DC Power [voltage=5]
  R1 = Resistor [tolerance=±5% resistance=220 package=THT]
  5V = DC Power [voltage=5]
  LED3 = RGB LED (com. cathode, rgb) [package="5 mm [THT]"]
  R2 = Resistor [tolerance=±5% resistance=220 package=THT]
  R3 = Resistor [tolerance=±5% resistance=220 package=THT]
  S2 = Square Pushbutton
  S3 = Square Pushbutton
  S4 = Square Pushbutton
  Display1 = LCD screen 16x2 IIC [part_number=101290]
  Pi_On_Off_Relay(SRD-05VDC-SL-C) = songle relay
  ZMCT103C = Current Sensor 5A
  ADS1115 = Adafruit ADS1115 16Bit I2C ADC [part_number="Adafruit #1085"]
  By-pass_switch(DPST_Switch) = SWITCH-DPDT [package=ms]
  Dry-Run_Relay(SRD-05VDC-SL-C) = songle relay

nets:
  VCC: MCU1.pin_2, MCU1.pin_4, GSM_SIM_GPSR_SMS_SIM900_SIM1.5V, BMS.V+, DC-DC.V+, Display1.VCC, Pi_On_Off_Relay(SRD-05VDC-SL-C).VCC, ZMCT103C.VCC, ADS1115.VDD, Dry-Run_Relay(SRD-05VDC-SL-C).VCC
  N1: MCU1.pin_3, Display1.SDA, ADS1115.SDA
  N2: MCU1.pin_5, Display1.SCL, ADS1115.SCL
  GND: MCU1.pin_6, MCU1.pin_9, MCU1.pin_14, MCU1.pin_39, GSM_SIM_GPSR_SMS_SIM900_SIM1.GND, BMS.V-, DC-DC.V-, Display1.GND, Pi_On_Off_Relay(SRD-05VDC-SL-C).GND, ZMCT103C.GND, ADS1115.GND, By-pass_switch(DPST_Switch).6, Dry-Run_Relay(SRD-05VDC-SL-C).GND
  N3: MCU1.pin_8, GSM_SIM_GPSR_SMS_SIM900_SIM1.SIM_RXD
  N4: MCU1.pin_10, GSM_SIM_GPSR_SMS_SIM900_SIM1.SIM_TXD
  N5: MCU1.pin_11, LED3.green_anode, R2.Pin_1
  N6: MCU1.pin_13, LED3.blue_anode, R3.Pin_1
  N7: MCU1.pin_15, R1.Pin_1, LED3.red_anode
  N8: MCU1.pin_23, By-pass_switch(DPST_Switch).5
  N9: R1.Pin_0, S2.leg1
  N10: 5V.V+, S2.leg0, S3.leg0, S4.leg0
  N11: 5V.V-, LED3.common_cathode
  N12: R2.Pin_0, S3.leg1
  N13: R3.Pin_0, S4.leg1
  N14: Pi_On_Off_Relay(SRD-05VDC-SL-C).NO, By-pass_switch(DPST_Switch).3
  N15: Pi_On_Off_Relay(SRD-05VDC-SL-C).COMMON, By-pass_switch(DPST_Switch).2, Dry-Run_Relay(SRD-05VDC-SL-C).NC
  N16: ZMCT103C.2, ZMCT103C.OUT, ADS1115.AIN0, Dry-Run_Relay(SRD-05VDC-SL-C).COMMON

notes:
  Phase monitor module
  Phase monitor

custom parts:
  LCD screen 16x2 IIC: LCD screen with HD44780 controller enables showing text, symbols, value or anything else that comes from Croduino/Arduino. It is capable of showing 16 symbols in two lines and therefore can be used in many projects that need to send clearly visible and legible output information.. • Color of symbols: White • Backlight: Blue • Dimensions: 80 x 36 x 12 mm • Screen dimensions: 64.5 x 16 mm •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
  Adafruit ADS1115 16Bit I2C ADC: For microcontrollers without an analog-to-digital converter or when you want a higher-precision ADC, the ADS1115 provides 16-bit precision at 860 samples/second over I2C. The chip can be configured as 4 single-ended input channels, or two differential channels. As a nice bonus, it even includes a programmable gain amplifier, up to x16, to help boost up smaller single/differential signals to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
