# Fritzing sketch Virtual_motor_auto_switch (saved by Fritzing 0.9.5d)
circuit board: 1.86337cm x 1.87216cm

parts:
  LED2 = LED - 5mm [color="Green (570nm)" package="5 mm [THT]"]
  R2 = Resistor [tolerance=±5% resistance=220 package=THT]
  S1 = Square Pushbutton
  V1 = DC Power [voltage=5]

nets:
  N1: LED2.cathode, V1.V-
  N2: LED2.anode, R2.Pin_0
  N3: R2.Pin_1, S1.leg0
  N4: S1.leg1, V1.V+
